# Fritzing sketch pcb (saved by Fritzing 0.9.3b)
circuit board: 7.60928cm x 4.81539cm
breadboards: 1

parts:
  J2 = Screw terminal - 2 pins [package=THT]
  J3 = Screw terminal - 2 pins [package=THT]
  R1 = Resistor [tolerance=±5% resistance=220 package=THT]
  R2 = Resistor [tolerance=±5% resistance=220 package=THT]
  J1 = Screw terminal - 2 pins [package=THT]
  Pad1 = Pad [width=3.0860106401246981 height=16.848657720211744 connect=center]  # not connected

nets:
  N1: J2.pin1, J3.pin1, J1.pin1
  N2: J2.pin2, R1.Pin_0
  N3: J3.pin2, R1.Pin_1, R2.Pin_1
  N4: R2.Pin_0, J1.pin2

notes:
  +
  -
